# Fritzing sketch Parallel1 (saved by Fritzing 0.9.4)
breadboards: 1

parts:
  R1 = Resistor [tolerance=±5% resistance=100 package=THT]
  LED2 = LED - 5mm [color="Red (633nm)" package="5 mm [THT]"]
  Part1 = Arduino Uno (Rev3)
  LED1 = LED - 5mm [color="Red (633nm)" package="5 mm [THT]"]

nets:
  N1: R1.Pin_0, LED2.cathode, LED1.cathode
  N2: R1.Pin_1, Part1.GND
  N3: LED2.anode, Part1.D6_PWM, LED1.anode
